// Logisim project FSM_Grid_Stabilityiteration_FINAL112233.XML (1).circ as structural Verilog: 1 circuit, main circuit main
module main (
  input  GRID_OK
);

  wire and_1_out, and_2_out, and_3_out, and_4_out, and_5_out, and_6_out, and_7_out, and_8_out, and_9_out,
       and_10_out, and_11_out, and_12_out, and_13_out, and_14_out, and_15_out, and_16_out, and_17_out,
       and_18_out, and_19_out, and_20_out, and_21_out, and_22_out, and_23_out, and_24_out, and_25_out,
       d_ff_1_q, FSM_CLK_out, not_1_out, not_2_out, not_3_out, not_4_out, not_5_out, or_1_out, or_2_out,
       or_3_out, or_4_out, or_5_out, or_6_out, S0_q, S0_qn, S1_q, S1_qn;
  wire [2:0] counter_05_q, counter_50_q;

  Clock FSM_CLK (.out(FSM_CLK_out));
  D_Flip_Flop S1 (.D(or_6_out), .clk(FSM_CLK_out), .Q(S1_q), .Qn(S1_qn), .preset(1'b0), .reset(1'b0));
  D_Flip_Flop S0 (.D(or_5_out), .clk(FSM_CLK_out), .Q(S0_q), .Qn(S0_qn), .preset(1'b0), .reset(1'b0));
  not not_1 (not_1_out, GRID_OK);
  D_Flip_Flop d_ff_1 (.D(GRID_OK), .clk(FSM_CLK_out), .Q(d_ff_1_q), .preset(1'b0), .reset(1'b0));  // open: Qn
  LED led_1 (.in(S1_q));
  LED led_2 (.in(S0_q));
  Counter #(.max('h7), .width(3)) counter_50 (
    .clr(not_1_out), .load(1'b0), .up(1'b1), .count(GRID_OK), .clk(FSM_CLK_out), .Q(counter_50_q));  // open: D, carry
  // Probe on S1_q
  // Probe on S0_q
  not not_2 (not_2_out, or_1_out);
  and and_1 (and_1_out, counter_50_q[1], counter_50_q[2]);
  and and_2 (and_2_out, counter_50_q[0], counter_50_q[2]);
  or or_1 (or_1_out, and_1_out, and_2_out);
  not not_3 (not_3_out, and_25_out);
  // Probe on or_1_out
  and and_3 (and_3_out, S1_qn, S0_qn);
  and and_4 (and_4_out, S1_q, S0_qn);
  and and_5 (and_5_out, S1_qn, S0_q);
  and and_6 (and_6_out, and_25_out, not_1_out);
  and and_7 (and_7_out, S1_q, S0_q);
  and and_8 (and_8_out, GRID_OK, not_2_out);
  and and_9 (and_9_out, S1_qn, S0_q);
  and and_10 (and_10_out, not_3_out, not_1_out);
  and and_11 (and_11_out, S1_q, S0_q);
  and and_12 (and_12_out, d_ff_1_q, not_1_out);
  LED led_3 (.in(or_1_out));
  and and_13 (and_13_out, and_3_out, not_1_out);
  and and_14 (and_14_out, and_4_out, GRID_OK);
  and and_15 (and_15_out, and_5_out, and_6_out);
  and and_16 (and_16_out, and_7_out, and_8_out);
  and and_17 (and_17_out, and_9_out, and_10_out);
  and and_18 (and_18_out, S1_q, S0_qn);
  and and_19 (and_19_out, and_11_out, not_2_out);
  and and_20 (and_20_out, S1_qn, S0_q);
  and and_21 (and_21_out, S1_qn, S0_qn);
  and and_22 (and_22_out, S1_q, S0_qn);
  and and_23 (and_23_out, S1_q, S0_q);
  LED led_4 (.in(and_15_out));
  LED led_5 (.in(and_16_out));
  LED led_6 (.in(and_12_out));
  // Probe on and_20_out
  LED led_7 (.in(and_20_out));
  // Probe on and_21_out
  LED led_8 (.in(and_21_out));
  // Probe on and_22_out
  LED led_9 (.in(and_22_out));
  // Probe on and_23_out
  LED led_10 (.in(and_23_out));
  // Probe on and_13_out
  LED led_11 (.in(and_13_out));
  // Probe on and_14_out
  LED led_12 (.in(and_14_out));
  // Probe on and_15_out
  // Probe on and_16_out
  // Probe on and_17_out
  LED led_13 (.in(and_17_out));
  // Probe on and_18_out
  LED led_14 (.in(and_18_out));
  // Probe on and_12_out
  Counter #(.max('h7), .width(3)) counter_05 (
    .clr(and_12_out), .load(1'b0), .up(1'b1), .count(not_1_out), .clk(FSM_CLK_out), .Q(counter_05_q));  // open: D, carry
  or or_2 (or_2_out, and_13_out, and_14_out);
  or or_3 (or_3_out, and_15_out, and_16_out);
  or or_4 (or_4_out, and_17_out, and_18_out);
  or or_5 (or_5_out, or_2_out, or_3_out);
  LED led_15 (.in(or_5_out));
  LED led_16 (.in(or_6_out));
  or or_6 (or_6_out, or_4_out, and_19_out);
  // Probe on or_5_out
  // Probe on or_6_out
  and and_24 (and_24_out, counter_05_q[1], counter_05_q[0]);
  not not_4 (not_4_out, and_24_out);
  not not_5 (not_5_out, counter_05_q[2]);
  and and_25 (and_25_out, not_4_out, not_5_out);
  // Probe on and_25_out
  LED led_17 (.in(and_25_out));

  // Notes on the sheet:
  //   N_S1
  //   N_S0
  //   GRID_OK_d 
endmodule
